# Fritzing sketch Sensor_de_luz_lcd (saved by Fritzing 0.9.0b)
breadboards: 1

parts:
  R1 = Resistor [tolerance=±5% resistance=10k package=THT]
  LCD1 = LCD screen
  R2 = Photocell (LDR) [package=THT]
  U1 = POT [package=pot_alpha_rv16af-20]
  Componente1 = Arduino Leonardo (Rev3b)

nets:
  VSS: R1.Pin_0, LCD1.VSS, LCD1.R/W, LCD1.LED-, U1.A, Componente1.GND
  N1: R1.Pin_1, R2.pin_0, Componente1.A0
  VDD: LCD1.VDD, LCD1.LED+, R2.pin_1, U1.E, Componente1.5V
  N2: LCD1.V0, U1.S
  N3: LCD1.RS, Componente1.D12/A11
  N4: LCD1.E, Componente1.D11_PWM
  N5: LCD1.DB4, Componente1.D5_PWM
  N6: LCD1.DB5, Componente1.D4/A6
  N7: LCD1.DB6, Componente1.D3_PWM/SCL, Componente1.SCL
  N8: LCD1.DB7, Componente1.D2/SDA, Componente1.SDA
